# Fritzing sketch project (saved by Fritzing 0.9.3b)
breadboards: 1

parts:
  Componente1 = Arduino Uno (Rev3)
  7_Segment1 = 7-Segment LED Display [package=THT]
  7_Segment2 = 7-Segment LED Display [package=THT]

nets:
  N1: Componente1.D8, 7_Segment2.cathodeB
  N2: Componente1.D9_PWM, 7_Segment2.cathodeC
  N3: Componente1.D10_PWM/SS, 7_Segment2.commAnode#2
  N4: Componente1.D11_PWM/MOSI, 7_Segment2.cathodeD
  N5: Componente1.D12/MISO, 7_Segment2.commAnode#7
  N6: Componente1.D13/SCK, 7_Segment2.cathodeF
  N7: Componente1.GND, 7_Segment1.cathodeF, 7_Segment1.cathodeG
  N8: Componente1.D0/RX, 7_Segment1.cathodeA
  N9: Componente1.D1/TX, 7_Segment1.cathodeB
  N10: Componente1.D2, 7_Segment1.cathodeC
  N11: Componente1.D3_PWM, 7_Segment1.cathodeD
  N12: Componente1.D4, 7_Segment1.cathodeE
  N13: Componente1.D5_PWM, 7_Segment1.commAnode#7
  N14: Componente1.D6_PWM, 7_Segment1.commAnode#2
  N15: Componente1.D7, 7_Segment2.cathodeA
